# Fritzing sketch mpu6050-raw (saved by Fritzing 0.9.3b)
breadboards: 1

parts:
  Arduino_Uno = Arduino Uno (Rev3) - ICSP
  MPU-6050_1 = InvenSense MPU6050
  MPU-6050_2 = InvenSense MPU6050

nets:
  N1: Arduino_Uno.A4/SDA, MPU-6050_1.SDA, MPU-6050_2.SDA
  N2: Arduino_Uno.A5/SCL, MPU-6050_1.SCL, MPU-6050_2.SCL
  N3: Arduino_Uno.D12/MISO, MPU-6050_2.AD0
  N4: Arduino_Uno.D13/SCK, MPU-6050_1.AD0
  VCC: Arduino_Uno.5V, MPU-6050_1.VCC, MPU-6050_2.VCC
  GND: Arduino_Uno.GND, MPU-6050_1.GND, MPU-6050_2.GND
